# Fritzing sketch ricevitore (saved by Fritzing 0.9.3b)
breadboards: 1

parts:
  R3 = Resistor [tolerance=±5% resistance=1k package=THT]
  Part5 = Adafruit Feather M0 RFM9x LoRa [part_number="Adafruit #3178 or #3179"]
  U1 = Vibration Motor- ROB-08449 [package=vibe-motor-10mm]
  S1 = Momentary Switch [package=ksa_sealed_tac_switch]
  NEOPIXEL2 = Neopixel Strip -- White (30/m)
  J1 = Piezo Speaker
  Q1 = TRANSISTOR_NPN [package=to-92]
  R4 = Resistor [tolerance=±5% resistance=1k package=THT]
  D1 = Zener Diode [part_number=1N4732A breakdown_voltage=3.6V package="Melf DO-213 AB [SMD]"]
  U2 = SWITCH_SPDT [package=kps-1290]

nets:
  N1: R3.Pin_0, Part5.A5, S1.4
  N2: Part5.A4, J1.pin2
  N3: Part5.A3, U2.P
  N4: Part5.VBAT, NEOPIXEL2.+5V
  N5: Part5.D9, NEOPIXEL2.Din
  N6: Part5.D6, R4.Pin_0
  N7: U1.+, Q1.E, D1.anode
  N8: U1.-, D1.cathode, U2.S
  N9: NEOPIXEL2.GND, J1.pin1, Q1.C, U2.O
  N10: Q1.B, R4.Pin_1

custom parts:
  Adafruit Feather M0 RFM9x LoRa: This is the Adafruit Feather M0 RFM95 LoRa Radio - our take on an microcontroller with a "Long Range (LoRa)" packet radio transceiver with built in USB and battery charging. Its an Adafruit Feather M0 with a 433Mhz or 900MHz radio module cooked in! Great for making wireless networks that are more flexible than Bluetooth LE and without the high power requirements of WiFi. We have other boards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
  Neopixel Strip -- White (30/m): These NeoPixel strips have 30 digitally-addressable pixel LEDs per meter and are very affordable and are only 12.5 mm wide, 10 mm if you remove the strip from the casing.
